// Logisim project diagramaFinal.circ as structural Verilog: 1 circuit, main circuit main
module main (
  input  SR,
  input  SP,
  input  SN,
  input  A,
  input  VL,
  input  B0,
  input  B1
);

  wire and_1_out, and_2_out, and_3_out, and_4_out, and_5_out, and_6_out, and_7_out, and_8_out, and_9_out,
       and_10_out, and_11_out, and_12_out, and_13_out, and_14_out, and_15_out, and_16_out, and_17_out,
       and_18_out, and_19_out, and_20_out, and_21_out, and_22_out, and_23_out, and_24_out, and_25_out,
       and_26_out, and_27_out, and_28_out, and_29_out, and_30_out, and_31_out, and_32_out, and_33_out,
       and_34_out, and_35_out, and_36_out, and_37_out, and_38_out, and_39_out, and_40_out, and_41_out,
       and_42_out, and_43_out, and_44_out, and_45_out, and_46_out, and_47_out, and_48_out, and_49_out,
       and_50_out, and_51_out, and_52_out, and_53_out, and_54_out, and_55_out, and_56_out, and_57_out,
       and_58_out, and_59_out, and_60_out, and_61_out, clock_1_out, D0_q, D1_q, D2_q, D3_q, or_1_out,
       or_2_out, or_3_out, or_4_out, or_5_out, or_6_out, or_7_out, or_8_out, or_9_out, or_10_out, or_11_out,
       or_12_out, or_13_out, or_14_out, or_15_out, or_16_out, or_17_out, or_18_out, or_19_out, or_20_out,
       or_21_out, or_22_out, or_23_out, or_24_out, or_25_out, xor_1_out, xor_2_out, xor_3_out;

  xor xor_1 (xor_1_out, D1_q, D0_q);
  and and_1 (and_1_out, ~D3_q, ~D1_q, ~D0_q, A, VL, B0, B1);  // AND_Gate
  and and_2 (and_2_out, or_6_out, ~D2_q, SR, SP, SN);  // AND_Gate
  or or_1 (or_1_out, D1_q, D0_q);
  and and_3 (and_3_out, or_1_out, ~D3_q, D2_q);  // AND_Gate
  and and_4 (and_4_out, D3_q, ~D2_q, ~D1_q, ~D0_q);  // AND_Gate
  and and_5 (and_5_out, SR, SP, SN);
  and and_6 (and_6_out, and_5_out, ~D2_q, A, ~VL);  // AND_Gate
  and and_7 (and_7_out, and_5_out, ~D2_q, A, VL, ~B0);  // AND_Gate
  and and_8 (and_8_out, and_5_out, ~D2_q, A, VL, B0, ~B1);  // AND_Gate
  and and_9 (and_9_out, or_2_out, ~D3_q, ~D1_q, ~D0_q);  // AND_Gate
  and and_10 (and_10_out, D2_q, VL);
  xor xor_2 (xor_2_out, B0, B1);
  and and_11 (and_11_out, xor_2_out, SP, SN, A, VL);
  and and_12 (and_12_out, SP, ~SN);  // AND_Gate
  and and_13 (and_13_out, or_4_out, ~D3_q, ~D2_q, ~D1_q, ~D0_q, SR);  // AND_Gate
  and and_14 (and_14_out, ~D0_q, ~SP);  // AND_Gate
  and and_15 (and_15_out, D0_q, ~SN);  // AND_Gate
  and and_16 (and_16_out, or_5_out, ~D3_q, ~D2_q, D1_q);  // AND_Gate
  xor xor_3 (xor_3_out, D1_q, D0_q);
  and and_17 (and_17_out, xor_3_out, and_5_out, D1_q, ~D0_q);  // AND_Gate
  and and_18 (and_18_out, xor_1_out, D3_q);
  or or_2 (or_2_out, and_6_out, and_7_out, and_8_out);
  or or_3 (or_3_out, and_9_out, and_10_out);
  or or_4 (or_4_out, and_11_out, ~SP, and_12_out);  // OR_Gate
  or or_5 (or_5_out, and_14_out, and_15_out);
  or or_6 (or_6_out, and_18_out, and_1_out);
  or or_7 (or_7_out, and_2_out, and_3_out, and_4_out);
  or or_8 (or_8_out, and_13_out, and_16_out, and_17_out);
  and and_19 (and_19_out, SR, SP, ~SN);  // AND_Gate
  and and_20 (and_20_out, SR, SP, SN, A, VL, ~B1);  // AND_Gate
  and and_21 (and_21_out, or_10_out, ~D3_q, ~D2_q, ~D1_q, ~D0_q);  // AND_Gate
  and and_22 (and_22_out, ~D3_q, ~D2_q, ~D1_q, D0_q, ~SR);  // AND_Gate
  and and_23 (and_23_out, ~D3_q, ~D2_q, D1_q, D0_q, ~SN);  // AND_Gate
  and and_24 (and_24_out, D3_q, ~D2_q, ~D0_q, SR, SP, SN);  // AND_Gate
  and and_25 (and_25_out, D3_q, ~D2_q, ~D1_q, ~D0_q);  // AND_Gate
  or or_9 (or_9_out, D1_q, D0_q);
  and and_26 (and_26_out, or_9_out, ~D3_q, D2_q);  // AND_Gate
  or or_10 (or_10_out, and_19_out, ~SR, and_20_out);  // OR_Gate
  or or_11 (or_11_out, and_21_out, and_22_out, and_23_out, and_24_out, and_25_out, and_26_out);
  Clock clock_1 (.out(clock_1_out));
  D_Flip_Flop D3 (.clk(clock_1_out), .D(or_7_out), .Q(D3_q));  // open: Qn, preset, en, reset
  D_Flip_Flop D2 (.clk(clock_1_out), .D(or_3_out), .Q(D2_q));  // open: Qn, preset, en, reset
  D_Flip_Flop D1 (.clk(clock_1_out), .D(or_8_out), .Q(D1_q));  // open: Qn, preset, en, reset
  D_Flip_Flop D0 (.clk(clock_1_out), .D(or_11_out), .Q(D0_q));  // open: Qn, preset, en, reset
  and and_27 (and_27_out, ~D3_q, ~D2_q, ~D1_q, ~SR);  // AND_Gate
  or or_12 (or_12_out, SR, D1_q);
  and and_28 (and_28_out, or_12_out, ~D3_q, ~D2_q, ~SP, ~D0_q);  // AND_Gate
  and and_29 (and_29_out, ~D1_q, ~D0_q, SR, SP);  // AND_Gate
  and and_30 (and_30_out, D1_q, D0_q);
  and and_31 (and_31_out, or_14_out, ~D3_q, ~D2_q, ~SN);  // AND_Gate
  and and_32 (and_32_out, SR, SP, SN, A);
  and and_33 (and_33_out, or_15_out, ~D3_q, ~D1_q, ~D0_q, ~VL);  // AND_Gate
  and and_34 (and_34_out, D2_q, D0_q);
  and and_35 (and_35_out, ~D2_q, ~D0_q, SR, SP, SN, A, VL, ~B0, ~B1);  // AND_Gate
  and and_36 (and_36_out, or_16_out, ~D3_q, ~D1_q);  // AND_Gate
  and and_37 (and_37_out, D2_q, D1_q);
  and and_38 (and_38_out, ~D2_q, ~D1_q, SR, SP, SN, A, VL, ~B0, B1);  // AND_Gate
  and and_39 (and_39_out, or_17_out, ~D3_q, ~D0_q);  // AND_Gate
  and and_40 (and_40_out, ~D3_q, ~D2_q, ~D1_q, ~D0_q, SR, SP, SN, A, VL, B0, ~B1);  // AND_Gate
  and and_41 (and_41_out, ~D3_q, D2_q, D1_q, D0_q);  // AND_Gate
  and and_42 (and_42_out, SR, SP, SN, A, VL, B0, B1);
  or or_13 (or_13_out, and_42_out, D3_q);
  and and_43 (and_43_out, or_13_out, ~D2_q, ~D1_q, ~D0_q);  // AND_Gate
  and and_44 (and_44_out, ~D1_q, D0_q);  // AND_Gate
  and and_45 (and_45_out, D1_q, ~D0_q);  // AND_Gate
  and and_46 (and_46_out, or_19_out, D3_q, ~D2_q, SR, SP, SN);  // AND_Gate
  and and_47 (and_47_out, D3_q, ~D2_q, D1_q, D0_q);  // AND_Gate
  or or_14 (or_14_out, and_29_out, and_30_out);
  or or_15 (or_15_out, and_32_out, D2_q);
  or or_16 (or_16_out, and_34_out, and_35_out);
  or or_17 (or_17_out, and_37_out, and_38_out);
  or or_18 (or_18_out, and_40_out, and_41_out);
  or or_19 (or_19_out, and_44_out, and_45_out);
  or or_20 (or_20_out, and_46_out, and_47_out);
  LED E0 (.in(and_27_out));
  LED E1 (.in(and_28_out));
  LED E2 (.in(and_31_out));
  LED E3 (.in(and_33_out));
  LED S0 (.in(and_36_out));
  LED S1 (.in(and_39_out));
  LED S2 (.in(or_18_out));
  LED S3 (.in(and_43_out));
  LED P (.in(or_20_out));
  LED AQ (.in(and_49_out));
  LED PP (.in(and_50_out));
  LED M (.in(or_25_out));
  and and_48 (and_48_out, SR, SP, SN);
  or or_21 (or_21_out, and_48_out, D0_q);
  and and_49 (and_49_out, or_21_out, D3_q, ~D2_q, D1_q);  // AND_Gate
  and and_50 (and_50_out, D3_q, ~D2_q, D1_q, D0_q);  // AND_Gate
  and and_51 (and_51_out, ~SR, SP, SN);  // AND_Gate
  and and_52 (and_52_out, SR, ~SP, SN);  // AND_Gate
  and and_53 (and_53_out, SR, SP, ~SN);  // AND_Gate
  and and_54 (and_54_out, or_23_out, D3_q, ~D2_q, D1_q, ~D0_q);  // AND_Gate
  and and_55 (and_55_out, or_23_out, D3_q, ~D2_q, ~D1_q, D0_q);  // AND_Gate
  and and_56 (and_56_out, ~D3_q, D2_q, ~D1_q, ~D0_q, VL);  // AND_Gate
  and and_57 (and_57_out, ~D0_q, SP);  // AND_Gate
  and and_58 (and_58_out, D0_q, SN);
  and and_59 (and_59_out, or_24_out, ~D3_q, ~D2_q, D1_q);  // AND_Gate
  and and_60 (and_60_out, SP, SN, ~A);  // AND_Gate
  or or_22 (or_22_out, and_60_out, D0_q);
  and and_61 (and_61_out, or_22_out, ~D3_q, ~D2_q, ~D1_q, SR);  // AND_Gate
  or or_23 (or_23_out, and_51_out, and_52_out, and_53_out);
  or or_24 (or_24_out, and_57_out, and_58_out);
  or or_25 (or_25_out, and_54_out, and_55_out, and_56_out, and_59_out, and_61_out);

  // Notes on the sheet:
  //   SR - SP - SN - A - VL - B0 - B1
  //   SR - SP - SN - A - VL - B0 - B1
  //   SR - SP - SN - A - VL - B0 - B1 - Q3 - Q2 - Q1 - Q0
  //   SR - SP - SN - A - VL - B0 - B1 - Q3 - Q2 - Q1 - Q0
  //   SR - SP - SN - A - VL - B0 - B1 - Q3 - Q2 - Q1 - Q0
  //   SR - SP - SN - A - VL - B0 - B1 - Q3 - Q2 - Q1 - Q0
endmodule
